// Logisim project GrandPa_test.circ as structural Verilog
module data_path (
  input  load,
  input  clk,
  input  shift,
  input  reset,
  input  [7:0] number
);

  wire A_p13, A_p14, A_p15, A_p16, A_p17, A_p18, A_p19, A_p20, and_1_out, square_ready;
  wire [7:0] neg_1_res;
  wire [15:0] adder_1_out, B_p18, R_q;

  neg neg_1 (.number(number), .negate(number[7]), .res(neg_1_res));
  // Shift_Register A: pin names not known; wires that end beside it: load, shift, clk, 1'b0, neg_1_res[7], neg_1_res[6], neg_1_res[5], neg_1_res[4], neg_1_res[3], neg_1_res[2], neg_1_res[1], neg_1_res[0], A_p13, A_p14, A_p15, A_p16, A_p17, A_p18, A_p19, A_p20
  nor nor_1 (square_ready, A_p13, A_p14, A_p15, A_p16, A_p17, A_p18, A_p19, A_p20);
  and and_1 (and_1_out, shift, A_p20);
  // Shift_Register #(.length(16)) B: pin names not known; wires that end beside it: 1'b0, load, shift, clk, 1'b0, neg_1_res[0], neg_1_res[1], neg_1_res[2], neg_1_res[3], neg_1_res[4], neg_1_res[5], neg_1_res[6], neg_1_res[7], neg_1_res[7], neg_1_res[7], neg_1_res[7], neg_1_res[7], B_p18[0], B_p18[1], B_p18[2], B_p18[3], B_p18[4], B_p18[5], B_p18[6], B_p18[7], B_p18[8], B_p18[9], B_p18[10], B_p18[11]
  Register #(.width(16)) R (.D(adder_1_out), .en(and_1_out), .clk(clk), .Q(R_q), .clr(reset));
  Adder #(.width(16)) adder_1 (.a(B_p18), .b(R_q), .out(adder_1_out));  // open: cin, cout
endmodule

module neg (
  input  [7:0] number,
  input  negate,
  output [7:0] res
);

  wire [7:0] xor_8_out;

  xor xor_1 (xor_8_out[7], number[7], negate);
  xor xor_2 (xor_8_out[6], number[6], negate);
  xor xor_3 (xor_8_out[5], number[5], negate);
  xor xor_4 (xor_8_out[4], number[4], negate);
  xor xor_5 (xor_8_out[3], number[3], negate);
  xor xor_6 (xor_8_out[2], number[2], negate);
  xor xor_7 (xor_8_out[1], number[1], negate);
  xor xor_8 (xor_8_out[0], number[0], negate);
  Adder adder_1 (.a(xor_8_out), .b({8{1'b0}}), .out(res), .cin(negate));  // open: cout
endmodule
